# Fritzing sketch Arduino Powerglove (saved by Fritzing 0.7.4b)
breadboards: 1

parts:
  Arduino1 = Arduino
  R1 = Resistor [tolerance=±5% resistance=1k package=THT]
  B1 = Pushbutton [package="[THT]"]
  B2 = Pushbutton [package="[THT]"]
  B3 = Pushbutton [package="[THT]"]
  B4 = Pushbutton [package="[THT]"]
  B5 = Pushbutton [package="[THT]"]
  R2 = Resistor [tolerance=±5% resistance=10k package=THT]
  R3 = Resistor [tolerance=±5% resistance=20k package=THT]
  R4 = Resistor [tolerance=±5% resistance=33k package=THT]
  R5 = Resistor [tolerance=±5% resistance=68k package=THT]
  R6 = Resistor [tolerance=±5% resistance=100k package=THT]

nets:
  N1: Arduino1.GND, R6.Pin_0
  N2: Arduino1.+5V, R1.Pin_1, R2.Pin_1, R3.Pin_1, R4.Pin_1, R5.Pin_1
  N3: Arduino1.A0, B1.Pin_3, B1.Pin_4, B2.Pin_3, B2.Pin_4, B3.Pin_3, B3.Pin_4, B4.Pin_3, B4.Pin_4, B5.Pin_3, B5.Pin_4, R6.Pin_1
  N4: R1.Pin_0, B1.Pin_1, B1.Pin_2
  N5: B2.Pin_1, B2.Pin_2, R2.Pin_0
  N6: B3.Pin_1, B3.Pin_2, R3.Pin_0
  N7: B4.Pin_1, B4.Pin_2, R4.Pin_0
  N8: B5.Pin_1, B5.Pin_2, R5.Pin_0
